// Logisim project Clock.circ as structural Verilog: 11 circuits, main circuit main
module main (
  input  in_1
);

  wire clock_1_out, clock_2_out, down_1_out_11, down_1_out_12, down_1_out_13, down_1_out_15, down_1_out_16,
       down_1_out_17, down_1_out_18, down_1_out_19, down_1_out_20, down_1_out_21, down_1_out_22,
       down_1_out_23, down_1_out_24, down_1_out_25, down_1_out_26, down_1_out_28, down_1_out_29,
       down_1_out_30, up_1_out_5, up_1_out_6, up_1_out_7, up_1_out_8, up_1_out_9, up_1_out_10, up_1_out_11,
       up_1_out_12, up_1_out_13, up_1_out_14, up_1_out_15, up_1_out_16, up_1_out_17, up_1_out_18,
       up_1_out_19, up_1_out_20, up_1_out_21, up_1_out_22, up_1_out_25, up_1_out_26, up_1_out_27,
       up_1_out_28, up_1_out_31, up_1_out_32;

  Clock clock_1 (.out(clock_1_out));
  Clock clock_2 (.out(clock_2_out));
  Up up_1 (
    .in_1(in_1), .in_2(in_1), .in_3(in_1), .in_4(clock_2_out), .out_16(up_1_out_16), .out_7(up_1_out_7),
    .out_17(up_1_out_17), .out_5(up_1_out_5), .out_18(up_1_out_18), .out_6(up_1_out_6), .out_19(up_1_out_19),
    .out_9(up_1_out_9), .out_10(up_1_out_10), .out_25(up_1_out_25), .out_11(up_1_out_11),
    .out_20(up_1_out_20), .out_12(up_1_out_12), .out_8(up_1_out_8), .out_21(up_1_out_21),
    .out_26(up_1_out_26), .out_27(up_1_out_27), .out_13(up_1_out_13), .out_28(up_1_out_28),
    .out_14(up_1_out_14), .out_22(up_1_out_22), .out_31(up_1_out_31), .out_15(up_1_out_15),
    .out_32(up_1_out_32));  // open: out_23, out_24, out_29, out_30
  _7_Segment_Display u_7_segment_display_1 (
    .g(up_1_out_16), .f(up_1_out_7), .a(up_1_out_17), .b(up_1_out_5), .e(down_1_out_18), .d(down_1_out_19),
    .c(down_1_out_25));  // open: dp
  _7_Segment_Display u_7_segment_display_2 (
    .g(up_1_out_18), .f(up_1_out_6), .a(up_1_out_19), .b(up_1_out_9), .e(down_1_out_20), .d(down_1_out_26),
    .c(down_1_out_12));  // open: dp
  Down down_1 (
    .in_1(in_1), .in_2(in_1), .in_3(in_1), .in_4(clock_2_out), .out_18(down_1_out_18),
    .out_19(down_1_out_19), .out_25(down_1_out_25), .out_20(down_1_out_20), .out_26(down_1_out_26),
    .out_12(down_1_out_12), .out_21(down_1_out_21), .out_17(down_1_out_17), .out_13(down_1_out_13),
    .out_22(down_1_out_22), .out_15(down_1_out_15), .out_23(down_1_out_23), .out_24(down_1_out_24),
    .out_16(down_1_out_16), .out_28(down_1_out_28), .out_29(down_1_out_29), .out_11(down_1_out_11),
    .out_30(down_1_out_30));  // open: out_27, out_5, out_7, out_9, out_31, out_10, out_8, out_6, out_32, out_14
  _7_Segment_Display u_7_segment_display_3 (
    .g(up_1_out_10), .f(up_1_out_25), .a(up_1_out_11), .b(up_1_out_20), .e(down_1_out_21), .d(down_1_out_17),
    .c(down_1_out_13));  // open: dp
  _7_Segment_Display u_7_segment_display_4 (
    .g(up_1_out_12), .f(up_1_out_8), .a(up_1_out_21), .b(up_1_out_26), .e(down_1_out_22), .d(down_1_out_15),
    .c(down_1_out_23));  // open: dp
  _7_Segment_Display u_7_segment_display_5 (
    .g(up_1_out_27), .f(up_1_out_13), .a(up_1_out_28), .b(up_1_out_14), .e(down_1_out_24), .d(down_1_out_16),
    .c(down_1_out_28));  // open: dp
  _7_Segment_Display u_7_segment_display_6 (
    .g(up_1_out_22), .f(up_1_out_31), .a(up_1_out_15), .b(up_1_out_32), .e(down_1_out_29), .d(down_1_out_11),
    .c(down_1_out_30));  // open: dp

  // Notes on the sheet:
  //   DIGITAL CLOCK
  //   2107115 & 2107116
endmodule

module up0_9 (
  input  in_1,
  input  in_2,
  input  in_3,
  output a,
  output b,
  output c,
  output d
);

  wire and_1_out, and_2_out, and_3_out, and_4_out, not_1_out, or_1_out;

  or or_1 (or_1_out, and_1_out, and_2_out);
  T_Flip_Flop t_ff_1 (.clk(in_1), .T(or_1_out), .Q(a));  // open: Qn, preset, reset, en
  and and_1 (and_1_out, b, c, d);
  and and_2 (and_2_out, a, d);
  T_Flip_Flop t_ff_2 (.clk(in_1), .T(and_4_out), .Q(b), .reset(in_2));  // open: Qn, preset, en
  and and_3 (and_3_out, not_1_out, d);
  not not_1 (not_1_out, a);
  T_Flip_Flop t_ff_3 (.clk(in_1), .T(and_3_out), .Q(c));  // open: Qn, preset, reset, en
  and and_4 (and_4_out, c, d);
  T_Flip_Flop t_ff_4 (.clk(in_1), .T(in_1), .Q(d), .preset(in_3));  // open: Qn, reset, en

  // Notes on the sheet:
  //   2107116
endmodule

module _0_5 (
  input  in_1,
  input  in_2,
  output a,
  output b,
  output c
);

  wire and_1_out, and_2_out, and_3_out, or_1_out, t_ff_1_qn;

  or or_1 (or_1_out, and_3_out, and_1_out);
  and and_1 (and_1_out, a, c);
  T_Flip_Flop t_ff_1 (.clk(in_1), .T(or_1_out), .Q(a), .Qn(t_ff_1_qn));  // open: preset, reset, en
  and and_2 (and_2_out, c, t_ff_1_qn);
  and and_3 (and_3_out, c, b);
  T_Flip_Flop t_ff_2 (.clk(in_1), .T(and_2_out), .Q(b), .reset(in_2));  // open: Qn, preset, en
  T_Flip_Flop t_ff_3 (.clk(in_1), .T(in_1), .Q(c));  // open: Qn, preset, reset, en

  // Notes on the sheet:
  //   2107116
endmodule

module BCD_7seG (
  input  in_1,
  input  in_2,
  input  in_3,
  input  in_4,
  output out_5,
  output out_6,
  output out_7,
  output out_8,
  output out_9,
  output out_10,
  output out_11
);

  wire and_1_out, and_2_out, and_3_out, and_4_out, and_5_out, and_6_out, and_7_out, not_1_out, not_2_out,
       not_3_out, xnor_1_out, xnor_2_out, xor_1_out;

  not not_1 (not_1_out, in_2);
  not not_2 (not_2_out, in_3);
  not not_3 (not_3_out, in_4);
  xnor xnor_1 (xnor_1_out, in_2, in_4);
  xnor xnor_2 (xnor_2_out, in_3, in_4);
  and and_1 (and_1_out, not_1_out, not_3_out);
  and and_2 (and_2_out, in_2, not_2_out, in_4);
  and and_3 (and_3_out, not_3_out, not_2_out);
  and and_4 (and_4_out, in_2, not_2_out);
  xor xor_1 (xor_1_out, in_2, in_3);
  and and_5 (and_5_out, not_1_out, in_3);
  and and_6 (and_6_out, in_3, not_3_out);
  and and_7 (and_7_out, not_3_out, in_2);
  or or_1 (out_5, xnor_1_out, in_3, in_1);
  or or_2 (out_6, xnor_2_out, not_1_out);
  or or_3 (out_7, in_2, not_2_out, in_4);
  or or_4 (out_8, and_1_out, and_5_out, and_6_out, and_2_out, in_1);
  or or_5 (out_9, and_6_out, and_1_out);
  or or_6 (out_10, and_3_out, and_7_out, and_4_out, in_1);
  or or_7 (out_11, in_1, and_7_out, xor_1_out);
  _7_Segment_Display u_7_segment_display_1 (
    .g(out_11), .f(out_10), .a(out_5), .b(out_6), .e(out_9), .d(out_8), .c(out_7));  // open: dp

  // Notes on the sheet:
  //   2107115
endmodule

module SECOND (
  input  in_1,
  input  in_2,
  output out_3,
  output out_4,
  output out_5,
  output out_6,
  output out_7,
  output out_8,
  output out_9,
  output out_10,
  output out_11,
  output out_12,
  output out_13,
  output out_14,
  output out_15,
  output out_16,
  output out_17
);

  wire and_1_out, and_2_out, and_3_out, n0_5_1_a, n0_5_1_b, n0_5_1_c, nor_1_out, not_1_out, up0_9_1_a,
       up0_9_1_b, up0_9_1_c, up0_9_1_d;

  _0_5 u_0_5_1 (.in_1(nor_1_out), .a(n0_5_1_a), .b(n0_5_1_b), .c(n0_5_1_c));  // open: in_2
  nor nor_1 (nor_1_out, up0_9_1_d, up0_9_1_c, up0_9_1_b, up0_9_1_a);
  up0_9 up0_9_1 (
    .in_1(in_2), .in_3(and_1_out), .a(up0_9_1_a), .b(up0_9_1_b), .c(up0_9_1_c), .d(up0_9_1_d));  // open: in_2
  nor nor_2 (out_3, n0_5_1_c, n0_5_1_b, n0_5_1_a);
  and and_1 (and_1_out, and_2_out, and_3_out);
  and and_2 (and_2_out, n0_5_1_a, n0_5_1_c);
  and and_3 (and_3_out, up0_9_1_b, not_1_out, up0_9_1_c);
  BCD_7seG bcd_7seg_1 (
    .in_1(in_1), .in_2(n0_5_1_a), .in_3(n0_5_1_b), .in_4(n0_5_1_c), .out_5(out_4), .out_6(out_5),
    .out_7(out_6), .out_8(out_7), .out_9(out_8), .out_10(out_9), .out_11(out_10));
  not not_1 (not_1_out, up0_9_1_d);
  BCD_7seG bcd_7seg_2 (
    .in_1(up0_9_1_a), .in_2(up0_9_1_b), .in_3(up0_9_1_c), .in_4(up0_9_1_d), .out_5(out_11), .out_6(out_12),
    .out_7(out_13), .out_8(out_14), .out_9(out_15), .out_10(out_16), .out_11(out_17));
  _7_Segment_Display u_7_segment_display_1 (
    .g(out_10), .f(out_9), .a(out_4), .b(out_5), .e(out_8), .d(out_7), .c(out_6));  // open: dp
  _7_Segment_Display u_7_segment_display_2 (
    .g(out_17), .f(out_16), .a(out_11), .b(out_12), .e(out_15), .d(out_14), .c(out_13));  // open: dp

  // Notes on the sheet:
  //   2107115
endmodule

module Hour (
  input  in_1,
  input  in_2,
  output out_3,
  output out_4,
  output out_5,
  output out_6,
  output out_7,
  output out_8,
  output out_9,
  output out_10,
  output out_11,
  output out_12,
  output out_13,
  output out_14,
  output out_15,
  output out_16
);

  wire and_1_out, and_2_out, n0_5_1_a, n0_5_1_b, n0_5_1_c, nor_1_out, not_1_out, up0_9_1_a, up0_9_1_b,
       up0_9_1_c, up0_9_1_d;

  _0_5 u_0_5_1 (.in_1(nor_1_out), .in_2(and_1_out), .a(n0_5_1_a), .b(n0_5_1_b), .c(n0_5_1_c));
  and and_1 (and_1_out, n0_5_1_b, and_2_out);
  nor nor_1 (nor_1_out, up0_9_1_d, up0_9_1_c, up0_9_1_b, up0_9_1_a);
  up0_9 up0_9_1 (
    .in_1(in_2), .in_2(and_1_out), .in_3(and_1_out), .a(up0_9_1_a), .b(up0_9_1_b), .c(up0_9_1_c),
    .d(up0_9_1_d));
  and and_2 (and_2_out, up0_9_1_d, not_1_out, up0_9_1_b);
  BCD_7seG bcd_7seg_1 (
    .in_1(in_1), .in_2(n0_5_1_a), .in_3(n0_5_1_b), .in_4(n0_5_1_c), .out_5(out_3), .out_6(out_4),
    .out_7(out_5), .out_8(out_6), .out_9(out_7), .out_10(out_8), .out_11(out_9));
  not not_1 (not_1_out, up0_9_1_c);
  BCD_7seG bcd_7seg_2 (
    .in_1(up0_9_1_a), .in_2(up0_9_1_b), .in_3(up0_9_1_c), .in_4(up0_9_1_d), .out_5(out_10), .out_6(out_11),
    .out_7(out_12), .out_8(out_13), .out_9(out_14), .out_10(out_15), .out_11(out_16));
  _7_Segment_Display u_7_segment_display_1 (
    .g(out_9), .f(out_8), .a(out_3), .b(out_4), .e(out_7), .d(out_6), .c(out_5));  // open: dp
  _7_Segment_Display u_7_segment_display_2 (
    .g(out_16), .f(out_15), .a(out_10), .b(out_11), .e(out_14), .d(out_13), .c(out_12));  // open: dp

  // Notes on the sheet:
  //   2107115
endmodule

module Final (
  input  in_1,
  input  in_2,
  input  in_3
);

  wire clock_1_out, hour_1_out_3, hour_1_out_4, hour_1_out_5, hour_1_out_6, hour_1_out_7, hour_1_out_8,
       hour_1_out_9, hour_1_out_10, hour_1_out_11, hour_1_out_12, hour_1_out_13, hour_1_out_14,
       hour_1_out_15, hour_1_out_16, second_1_out_3, second_1_out_4, second_1_out_5, second_1_out_6,
       second_1_out_7, second_1_out_8, second_1_out_9, second_1_out_10, second_1_out_11, second_1_out_12,
       second_1_out_13, second_1_out_14, second_1_out_15, second_1_out_16, second_1_out_17, second_2_out_3,
       second_2_out_4, second_2_out_5, second_2_out_6, second_2_out_7, second_2_out_8, second_2_out_9,
       second_2_out_10, second_2_out_11, second_2_out_12, second_2_out_13, second_2_out_14, second_2_out_15,
       second_2_out_16, second_2_out_17;

  Clock clock_1 (.out(clock_1_out));
  Hour hour_1 (
    .in_1(in_1), .in_2(second_1_out_3), .out_3(hour_1_out_3), .out_4(hour_1_out_4), .out_5(hour_1_out_5),
    .out_6(hour_1_out_6), .out_7(hour_1_out_7), .out_8(hour_1_out_8), .out_9(hour_1_out_9),
    .out_10(hour_1_out_10), .out_11(hour_1_out_11), .out_12(hour_1_out_12), .out_13(hour_1_out_13),
    .out_14(hour_1_out_14), .out_15(hour_1_out_15), .out_16(hour_1_out_16));
  SECOND second_1 (
    .in_1(in_2), .in_2(second_2_out_3), .out_3(second_1_out_3), .out_4(second_1_out_4),
    .out_5(second_1_out_5), .out_6(second_1_out_6), .out_7(second_1_out_7), .out_8(second_1_out_8),
    .out_9(second_1_out_9), .out_10(second_1_out_10), .out_11(second_1_out_11), .out_12(second_1_out_12),
    .out_13(second_1_out_13), .out_14(second_1_out_14), .out_15(second_1_out_15), .out_16(second_1_out_16),
    .out_17(second_1_out_17));
  SECOND second_2 (
    .in_1(in_3), .in_2(clock_1_out), .out_3(second_2_out_3), .out_4(second_2_out_4), .out_5(second_2_out_5),
    .out_6(second_2_out_6), .out_7(second_2_out_7), .out_8(second_2_out_8), .out_9(second_2_out_9),
    .out_10(second_2_out_10), .out_11(second_2_out_11), .out_12(second_2_out_12), .out_13(second_2_out_13),
    .out_14(second_2_out_14), .out_15(second_2_out_15), .out_16(second_2_out_16), .out_17(second_2_out_17));
  _7_Segment_Display u_7_segment_display_1 (
    .g(hour_1_out_9), .f(hour_1_out_8), .a(hour_1_out_3), .b(hour_1_out_4), .e(hour_1_out_7),
    .d(hour_1_out_6), .c(hour_1_out_5));  // open: dp
  _7_Segment_Display u_7_segment_display_2 (
    .g(hour_1_out_16), .f(hour_1_out_15), .a(hour_1_out_10), .b(hour_1_out_11), .e(hour_1_out_14),
    .d(hour_1_out_13), .c(hour_1_out_12));  // open: dp
  _7_Segment_Display u_7_segment_display_3 (
    .g(second_1_out_17), .f(second_1_out_16), .a(second_1_out_11), .b(second_1_out_12), .e(second_1_out_15),
    .d(second_1_out_14), .c(second_1_out_13));  // open: dp
  _7_Segment_Display u_7_segment_display_4 (
    .g(second_1_out_10), .f(second_1_out_9), .a(second_1_out_4), .b(second_1_out_5), .e(second_1_out_8),
    .d(second_1_out_7), .c(second_1_out_6));  // open: dp
  _7_Segment_Display u_7_segment_display_5 (
    .g(second_2_out_10), .f(second_2_out_9), .a(second_2_out_4), .b(second_2_out_5), .e(second_2_out_8),
    .d(second_2_out_7), .c(second_2_out_6));  // open: dp
  _7_Segment_Display u_7_segment_display_6 (
    .g(second_2_out_17), .f(second_2_out_16), .a(second_2_out_11), .b(second_2_out_12), .e(second_2_out_15),
    .d(second_2_out_14), .c(second_2_out_13));  // open: dp

  // Notes on the sheet:
  //   HOUR
  //   MINUTE
  //   SECOND
  //   2107115
endmodule

module Final2 (
  input  in_1
);

  wire clock_1_out, down_1_out_11, down_1_out_12, down_1_out_13, down_1_out_15, down_1_out_16, down_1_out_17,
       down_1_out_18, down_1_out_19, down_1_out_20, down_1_out_21, down_1_out_22, down_1_out_23,
       down_1_out_24, down_1_out_25, down_1_out_26, down_1_out_28, down_1_out_29, down_1_out_30, up_1_out_5,
       up_1_out_6, up_1_out_7, up_1_out_8, up_1_out_9, up_1_out_10, up_1_out_11, up_1_out_12, up_1_out_13,
       up_1_out_14, up_1_out_15, up_1_out_16, up_1_out_17, up_1_out_18, up_1_out_19, up_1_out_20,
       up_1_out_21, up_1_out_22, up_1_out_25, up_1_out_26, up_1_out_27, up_1_out_28, up_1_out_31, up_1_out_32;

  Clock clock_1 (.out(clock_1_out));
  Up up_1 (
    .in_1(in_1), .in_2(in_1), .in_3(in_1), .in_4(clock_1_out), .out_16(up_1_out_16), .out_7(up_1_out_7),
    .out_17(up_1_out_17), .out_5(up_1_out_5), .out_18(up_1_out_18), .out_6(up_1_out_6), .out_19(up_1_out_19),
    .out_9(up_1_out_9), .out_10(up_1_out_10), .out_25(up_1_out_25), .out_11(up_1_out_11),
    .out_20(up_1_out_20), .out_12(up_1_out_12), .out_8(up_1_out_8), .out_21(up_1_out_21),
    .out_26(up_1_out_26), .out_27(up_1_out_27), .out_13(up_1_out_13), .out_28(up_1_out_28),
    .out_14(up_1_out_14), .out_22(up_1_out_22), .out_31(up_1_out_31), .out_15(up_1_out_15),
    .out_32(up_1_out_32));  // open: out_23, out_24, out_29, out_30
  _7_Segment_Display u_7_segment_display_1 (
    .g(up_1_out_16), .f(up_1_out_7), .a(up_1_out_17), .b(up_1_out_5), .e(down_1_out_18), .d(down_1_out_19),
    .c(down_1_out_25));  // open: dp
  _7_Segment_Display u_7_segment_display_2 (
    .g(up_1_out_18), .f(up_1_out_6), .a(up_1_out_19), .b(up_1_out_9), .e(down_1_out_20), .d(down_1_out_26),
    .c(down_1_out_12));  // open: dp
  Down down_1 (
    .in_1(in_1), .in_2(in_1), .in_3(in_1), .in_4(clock_1_out), .out_18(down_1_out_18),
    .out_19(down_1_out_19), .out_25(down_1_out_25), .out_20(down_1_out_20), .out_26(down_1_out_26),
    .out_12(down_1_out_12), .out_21(down_1_out_21), .out_17(down_1_out_17), .out_13(down_1_out_13),
    .out_22(down_1_out_22), .out_15(down_1_out_15), .out_23(down_1_out_23), .out_24(down_1_out_24),
    .out_16(down_1_out_16), .out_28(down_1_out_28), .out_29(down_1_out_29), .out_11(down_1_out_11),
    .out_30(down_1_out_30));  // open: out_27, out_5, out_7, out_9, out_31, out_10, out_8, out_6, out_32, out_14
  _7_Segment_Display u_7_segment_display_3 (
    .g(up_1_out_10), .f(up_1_out_25), .a(up_1_out_11), .b(up_1_out_20), .e(down_1_out_21), .d(down_1_out_17),
    .c(down_1_out_13));  // open: dp
  _7_Segment_Display u_7_segment_display_4 (
    .g(up_1_out_27), .f(up_1_out_13), .a(up_1_out_28), .b(up_1_out_14), .e(down_1_out_24), .d(down_1_out_16),
    .c(down_1_out_28));  // open: dp
  _7_Segment_Display u_7_segment_display_5 (
    .g(up_1_out_12), .f(up_1_out_8), .a(up_1_out_21), .b(up_1_out_26), .e(down_1_out_22), .d(down_1_out_15),
    .c(down_1_out_23));  // open: dp
  _7_Segment_Display u_7_segment_display_6 (
    .g(up_1_out_22), .f(up_1_out_31), .a(up_1_out_15), .b(up_1_out_32), .e(down_1_out_29), .d(down_1_out_11),
    .c(down_1_out_30));  // open: dp
endmodule

module Up (
  input  in_1,
  input  in_2,
  input  in_3,
  input  in_4,
  output out_5,
  output out_6,
  output out_7,
  output out_8,
  output out_9,
  output out_10,
  output out_11,
  output out_12,
  output out_13,
  output out_14,
  output out_15,
  output out_16,
  output out_17,
  output out_18,
  output out_19,
  output out_20,
  output out_21,
  output out_22,
  output out_23,
  output out_24,
  output out_25,
  output out_26,
  output out_27,
  output out_28,
  output out_29,
  output out_30,
  output out_31,
  output out_32
);

  wire hour_1_out_5, hour_1_out_6, hour_1_out_7, hour_1_out_12, hour_1_out_13, hour_1_out_14,
       second116_1_out_3, second116_1_out_6, second116_1_out_7, second116_1_out_8, second116_1_out_13,
       second116_1_out_14, second116_1_out_15, second_1_out_3, second_1_out_6, second_1_out_7,
       second_1_out_8, second_1_out_13, second_1_out_14, second_1_out_15;

  Hour hour_1 (
    .in_1(in_1), .in_2(second_1_out_3), .out_3(out_17), .out_4(out_5), .out_5(hour_1_out_5),
    .out_6(hour_1_out_6), .out_7(hour_1_out_7), .out_8(out_7), .out_9(out_16), .out_10(out_19),
    .out_11(out_9), .out_12(hour_1_out_12), .out_13(hour_1_out_13), .out_14(hour_1_out_14), .out_15(out_6),
    .out_16(out_18));
  SECOND second_1 (
    .in_1(in_2), .in_2(second116_1_out_3), .out_3(second_1_out_3), .out_4(out_11), .out_5(out_20),
    .out_6(second_1_out_6), .out_7(second_1_out_7), .out_8(second_1_out_8), .out_9(out_25), .out_10(out_10),
    .out_11(out_21), .out_12(out_26), .out_13(second_1_out_13), .out_14(second_1_out_14),
    .out_15(second_1_out_15), .out_16(out_8), .out_17(out_12));
  second116 second116_1 (
    .in_1(in_3), .in_2(in_4), .out_3(second116_1_out_3), .out_4(out_28), .out_5(out_14),
    .out_6(second116_1_out_6), .out_7(second116_1_out_7), .out_8(second116_1_out_8), .out_9(out_13),
    .out_10(out_27), .out_11(out_15), .out_12(out_32), .out_13(second116_1_out_13),
    .out_14(second116_1_out_14), .out_15(second116_1_out_15), .out_16(out_31), .out_17(out_22));

  assign out_23 = out_18;
  assign out_24 = out_20;
  assign out_29 = out_12;
  assign out_30 = out_14;
endmodule

module Down (
  input  in_1,
  input  in_2,
  input  in_3,
  input  in_4,
  output out_5,
  output out_6,
  output out_7,
  output out_8,
  output out_9,
  output out_10,
  output out_11,
  output out_12,
  output out_13,
  output out_14,
  output out_15,
  output out_16,
  output out_17,
  output out_18,
  output out_19,
  output out_20,
  output out_21,
  output out_22,
  output out_23,
  output out_24,
  output out_25,
  output out_26,
  output out_27,
  output out_28,
  output out_29,
  output out_30,
  output out_31,
  output out_32
);

  wire hour_1_out_3, hour_1_out_4, hour_1_out_8, hour_1_out_9, hour_1_out_11, hour_1_out_15, hour_1_out_16,
       second_1_out_3, second_1_out_10, second_1_out_12, second_2_out_3, second_2_out_4, second_2_out_5,
       second_2_out_9, second_2_out_10, second_2_out_16, second_2_out_17;

  Hour hour_1 (
    .in_1(in_1), .in_2(second_1_out_3), .out_3(hour_1_out_3), .out_4(hour_1_out_4), .out_5(out_25),
    .out_6(out_19), .out_7(out_18), .out_8(hour_1_out_8), .out_9(hour_1_out_9), .out_10(out_27),
    .out_11(hour_1_out_11), .out_12(out_12), .out_13(out_26), .out_14(out_20), .out_15(hour_1_out_15),
    .out_16(hour_1_out_16));
  SECOND second_1 (
    .in_1(in_2), .in_2(second_2_out_3), .out_3(second_1_out_3), .out_4(out_7), .out_5(out_5), .out_6(out_13),
    .out_7(out_17), .out_8(out_21), .out_9(out_9), .out_10(second_1_out_10), .out_11(out_10),
    .out_12(second_1_out_12), .out_13(out_23), .out_14(out_15), .out_15(out_22), .out_16(out_8),
    .out_17(out_6));
  SECOND second_2 (
    .in_1(in_3), .in_2(in_4), .out_3(second_2_out_3), .out_4(second_2_out_4), .out_5(second_2_out_5),
    .out_6(out_28), .out_7(out_16), .out_8(out_24), .out_9(second_2_out_9), .out_10(second_2_out_10),
    .out_11(out_32), .out_12(out_14), .out_13(out_30), .out_14(out_11), .out_15(out_29),
    .out_16(second_2_out_16), .out_17(second_2_out_17));

  assign out_31 = out_10;
endmodule

module second116 (
  input  in_1,
  input  in_2,
  output out_3,
  output out_4,
  output out_5,
  output out_6,
  output out_7,
  output out_8,
  output out_9,
  output out_10,
  output out_11,
  output out_12,
  output out_13,
  output out_14,
  output out_15,
  output out_16,
  output out_17
);

  wire and_1_out, and_2_out, and_3_out, and_4_out, n0_5_1_a, n0_5_1_b, n0_5_1_c, nor_1_out, not_1_out,
       up0_9_1_a, up0_9_1_b, up0_9_1_c, up0_9_1_d;

  nor nor_1 (nor_1_out, up0_9_1_c, up0_9_1_d, up0_9_1_a, up0_9_1_b);
  _0_5 u_0_5_1 (.in_1(nor_1_out), .a(n0_5_1_a), .b(n0_5_1_b), .c(n0_5_1_c));  // open: in_2
  and and_1 (and_1_out, n0_5_1_a, n0_5_1_c);
  up0_9 up0_9_1 (
    .in_1(in_2), .in_3(and_4_out), .a(up0_9_1_a), .b(up0_9_1_b), .c(up0_9_1_c), .d(up0_9_1_d));  // open: in_2
  nor nor_2 (out_3, n0_5_1_a, n0_5_1_b, n0_5_1_c);
  not not_1 (not_1_out, up0_9_1_d);
  and and_2 (and_2_out, up0_9_1_b, up0_9_1_c);
  and and_3 (and_3_out, not_1_out, and_2_out);
  and and_4 (and_4_out, and_1_out, and_3_out);
  BCD_7seG bcd_7seg_1 (
    .in_1(in_1), .in_2(n0_5_1_a), .in_3(n0_5_1_b), .in_4(n0_5_1_c), .out_5(out_4), .out_6(out_5),
    .out_7(out_6), .out_8(out_7), .out_9(out_8), .out_10(out_9), .out_11(out_10));
  BCD_7seG bcd_7seg_2 (
    .in_1(up0_9_1_a), .in_2(up0_9_1_b), .in_3(up0_9_1_c), .in_4(up0_9_1_d), .out_5(out_11), .out_6(out_12),
    .out_7(out_13), .out_8(out_14), .out_9(out_15), .out_10(out_16), .out_11(out_17));
  _7_Segment_Display u_7_segment_display_1 (
    .g(out_17), .f(out_16), .a(out_11), .b(out_12), .e(out_15), .d(out_14), .c(out_13));  // open: dp
  _7_Segment_Display u_7_segment_display_2 (
    .g(out_10), .f(out_9), .a(out_4), .b(out_5), .e(out_8), .d(out_7), .c(out_6));  // open: dp

  // Notes on the sheet:
  //   2107116
endmodule
